# Fritzing sketch sensor prox (saved by Fritzing 0.9.3b)
circuit board: 3cm x 4.5cm
circuit board: 4.5cm x 4.5cm
breadboards: 1

parts:
  LED1 = LED - 5mm [color="Red (633nm)" package="5 mm [THT]"]
  LED2 = LED - 5mm [color="Red (633nm)" package="5 mm [THT]"]
  LED3 = LED - 5mm [color="Red (633nm)" package="5 mm [THT]"]
  LED4 = LED - 5mm [color="Red (633nm)" package="5 mm [THT]"]
  LED5 = LED - 5mm [color="Red (633nm)" package="5 mm [THT]"]
  LED6 = LED - 5mm [color="Red (633nm)" package="5 mm [THT]"]
  J1 = Piezo Speaker
  Q1 = NPN-Transistor [package="TO92 [THT]"]
  U1 = ATTINY13 [package=dip]
  Q2 = NPN-Transistor [package="TO92 [THT]"]
  J2 = female pin header, 9 pins [form="♀ (female)"]
  C1 = Ceramic Capacitor [capacitance=100nF package="100 mil [THT, multilayer]"]
  J3 = female alternating pin header, 5 pins [form="♀ (female)"]
  LED7 = LED - 5mm [color="Red (633nm)" package="5 mm [THT]"]
  LED8 = LED - 5mm [color="Red (633nm)" package="5 mm [THT]"]
  R1 = Resistor [tolerance=±5% resistance=220 package=THT]
  R2 = Resistor [tolerance=±5% resistance=220 package=THT]
  R3 = Resistor [tolerance=±5% resistance=220 package=THT]
  LED9 = LED - 3mm [color="Red (633nm)" package="3 mm [THT]"]

nets:
  N1: LED1.cathode, LED2.cathode, LED3.cathode, J3.pin2, LED8.cathode
  N2: LED1.anode, LED2.anode, LED3.anode, LED4.anode, LED5.anode, LED6.anode, J3.pin5, LED7.anode, LED8.anode
  N3: LED4.cathode, LED5.cathode, LED6.cathode, J3.pin1, LED7.cathode
  N4: J1.pin1, J3.pin4
  N5: J1.pin2, J3.pin3
  N6: Q1.E, R1.Pin_0
  N7: Q1.B, U1.PB1(MISO)
  N8: Q1.C, U1.PB5(NRES), Q2.C, J2.pin2, J2.pin8, C1.0, LED9.cathode
  N9: U1.PB3(ADC3), J2.pin3
  N10: U1.PB4(ADC2), J2.pin4
  N11: U1.PB0(MOSI), J2.pin1, J2.pin9, C1.1, R3.Pin_0
  N12: U1.PB2(SCK_ADC1), Q2.B
  N13: U1.VCC, J2.pin7
  N14: Q2.E, R2.Pin_1
  N15: J2.pin5, R1.Pin_1
  N16: J2.pin6, R2.Pin_0
  N17: R3.Pin_1, LED9.anode

notes:
  + - T E R V B - +
  R V B - +
